// Logisim project Cache.circ as structural Verilog: 2 circuits, main circuit main
module main (
  input  Clock,
  input  [15:0] Address,
  output [31:0] Data_out,
  output [7:0] Byte
);

  wire cacheline_2_hit, cacheline_4_hit, cacheline_6_hit, cacheline_8_hit, demultiplexer_1_out0,
       demultiplexer_1_out1, demultiplexer_1_out2, demultiplexer_1_out3;
  wire [31:0] cacheline_1_data_out, cacheline_2_data_out, cacheline_3_data_out, cacheline_4_data_out,
       cacheline_5_data_out, cacheline_6_data_out, cacheline_7_data_out, cacheline_8_data_out,
       demultiplexer_2_out0, demultiplexer_2_out1, demultiplexer_2_out2, demultiplexer_2_out3,
       Main_Memory_data, multiplexer_1_out, multiplexer_2_out, multiplexer_3_out, multiplexer_4_out;

  Demultiplexer #(.select(2), .enable("false")) demultiplexer_1 (
    .out0(demultiplexer_1_out0), .out1(demultiplexer_1_out1), .out2(demultiplexer_1_out2),
    .out3(demultiplexer_1_out3), .in(Clock), .sel(Address[1:0]));
  ROM #(.addrWidth(16), .dataWidth(32), .Select("high")) Main_Memory (.addr(Address), .data(Main_Memory_data));
  CacheLine cacheline_1 (
    .Data_in(Main_Memory_data), .TAG(Address[13:2]), .Clock(demultiplexer_1_out0),
    .Data_out(cacheline_1_data_out));  // open: Hit
  CacheLine cacheline_2 (
    .Data_in(Main_Memory_data), .TAG(Address[13:2]), .Clock(demultiplexer_1_out0),
    .Data_out(cacheline_2_data_out), .Hit(cacheline_2_hit));
  CacheLine cacheline_3 (
    .Data_in(Main_Memory_data), .TAG(Address[13:2]), .Clock(demultiplexer_1_out1),
    .Data_out(cacheline_3_data_out));  // open: Hit
  CacheLine cacheline_4 (
    .Data_in(Main_Memory_data), .TAG(Address[13:2]), .Clock(demultiplexer_1_out1),
    .Data_out(cacheline_4_data_out), .Hit(cacheline_4_hit));
  CacheLine cacheline_5 (
    .Data_in(Main_Memory_data), .TAG(Address[13:2]), .Clock(demultiplexer_1_out2),
    .Data_out(cacheline_5_data_out));  // open: Hit
  CacheLine cacheline_6 (
    .Data_in(Main_Memory_data), .TAG(Address[13:2]), .Clock(demultiplexer_1_out2),
    .Data_out(cacheline_6_data_out), .Hit(cacheline_6_hit));
  CacheLine cacheline_7 (
    .Data_in(Main_Memory_data), .TAG(Address[13:2]), .Clock(demultiplexer_1_out3),
    .Data_out(cacheline_7_data_out));  // open: Hit
  CacheLine cacheline_8 (
    .Data_in(Main_Memory_data), .TAG(Address[13:2]), .Clock(demultiplexer_1_out3),
    .Data_out(cacheline_8_data_out), .Hit(cacheline_8_hit));
  Multiplexer #(.width(32), .enable("false")) multiplexer_1 (
    .in0(cacheline_1_data_out), .in1(cacheline_2_data_out), .out(multiplexer_1_out), .sel(cacheline_2_hit));
  Multiplexer #(.width(32), .enable("false")) multiplexer_2 (
    .in0(cacheline_3_data_out), .in1(cacheline_4_data_out), .out(multiplexer_2_out), .sel(cacheline_4_hit));
  Multiplexer #(.width(32), .enable("false")) multiplexer_3 (
    .in0(cacheline_5_data_out), .in1(cacheline_6_data_out), .out(multiplexer_3_out), .sel(cacheline_6_hit));
  Multiplexer #(.width(32), .enable("false")) multiplexer_4 (
    .in0(cacheline_7_data_out), .in1(cacheline_8_data_out), .out(multiplexer_4_out), .sel(cacheline_8_hit));
  Multiplexer #(.select(2), .width(32), .enable("false")) multiplexer_5 (
    .in0(multiplexer_1_out), .in1(multiplexer_2_out), .in2(multiplexer_3_out), .in3(multiplexer_4_out),
    .out(Data_out), .sel(Address[1:0]));
  Demultiplexer #(.select(2), .width(32), .enable("false")) demultiplexer_2 (
    .out0(demultiplexer_2_out0), .out1(demultiplexer_2_out1), .out2(demultiplexer_2_out2),
    .out3(demultiplexer_2_out3), .in(Data_out), .sel(Address[15:14]));
  Multiplexer #(.select(2), .width(8), .enable("false")) multiplexer_6 (
    .in0(demultiplexer_2_out0[7:0]), .in1(demultiplexer_2_out1[15:8]), .in2(demultiplexer_2_out2[23:16]),
    .in3(demultiplexer_2_out3[31:24]), .out(Byte), .sel(Address[15:14]));

  // Notes on the sheet:
  //   Set / Tag / Offset
  //   Set Selector
  //   contents of Main_Memory (hex, n*v repeats v):
  //   11112222 33334444 1111 22223333 10101010 10101010
  //   Cache
endmodule

module CacheLine (
  input  [31:0] Data_in,
  input  [11:0] TAG,
  input  Clock,
  output [31:0] Data_out,
  output Hit
);

  wire [31:0] multiplexer_1_out;

  Register #(.width(32), .Select("low")) Line_Data (.D(multiplexer_1_out), .Q(Data_out), .clk(Clock));  // open: en, clr
  Multiplexer #(.width(32), .enable("false")) multiplexer_1 (
    .in0(Data_in), .in1(Data_out), .out(multiplexer_1_out), .sel(Hit));
  Comparator #(.width(12)) comparator_1 (.a(Data_out[11:0]), .b(TAG), .eq(Hit));  // open: gt, lt
endmodule
