// Logisim project CacheLine.circ as structural Verilog: 1 circuit, main circuit main
module main (
  input  [31:0] Data_in,
  input  [11:0] TAG,
  input  Clock,
  output [31:0] Data_out,
  output Hit
);

  wire [31:0] multiplexer_1_out;

  Register #(.width(32), .Select("low")) Line_Data (.D(multiplexer_1_out), .Q(Data_out), .clk(Clock));  // open: en, clr
  Multiplexer #(.width(32), .enable("false")) multiplexer_1 (
    .in0(Data_in), .in1(Data_out), .out(multiplexer_1_out), .sel(Hit));
  Comparator #(.width(12)) comparator_1 (.a(Data_out[11:0]), .b(TAG), .eq(Hit));  // open: gt, lt
endmodule
