// Logisim project ControlUnit.circ as structural Verilog
module ControlUnit (
  input  [31:0] instr,
  output [3:0] ALUOp,
  output ALUSrc,
  output RegWrite,
  output MemToReg,
  output PCSrc,
  output Jump,
  output MemWrite,
  output MemRead
);

  wire and_1_out, and_2_out, and_3_out, and_4_out, and_5_out, and_6_out, and_7_out, and_8_out, and_9_out,
       and_10_out, and_11_out, and_12_out, and_13_out, and_14_out;

  and and_1 (and_1_out, instr[0], instr[1], ~instr[2], ~instr[3]);  // AND_Gate
  and and_2 (and_2_out, instr[4], instr[5], ~instr[6]);  // AND_Gate
  and and_3 (and_3_out, instr[4], ~instr[5], ~instr[6]);  // AND_Gate
  and and_4 (and_4_out, ~instr[4], ~instr[5], ~instr[6]);  // AND_Gate
  and and_5 (and_5_out, ~instr[4], instr[5], ~instr[6]);  // AND_Gate
  and and_6 (and_6_out, ~instr[4], instr[5], instr[6]);  // AND_Gate
  and and_7 (and_7_out, ~instr[4], instr[5], instr[6]);  // AND_Gate
  and and_8 (and_8_out, instr[0], instr[1], instr[2], instr[3]);
  and and_9 (and_9_out, and_1_out, and_2_out);
  and and_10 (and_10_out, and_1_out, and_3_out);
  and and_11 (and_11_out, and_1_out, and_4_out);
  and and_12 (and_12_out, and_1_out, and_5_out);
  and and_13 (and_13_out, and_1_out, and_6_out);
  and and_14 (and_14_out, and_7_out, and_8_out);
  Multiplexer #(.select(3), .enable("false")) multiplexer_1 (
    .in0(and_11_out), .in1(and_10_out), .in2(1'b0), .in3(and_9_out), .in4(1'b0), .in5(1'b0), .in6(1'b0),
    .in7(1'b0), .out(RegWrite), .sel(instr[6:4]));
  Multiplexer #(.select(3), .enable("false")) multiplexer_2 (
    .in0(and_11_out), .in1(and_10_out), .in2(and_12_out), .in3(1'b0), .in4(1'b0), .in5(1'b0),
    .in6(and_13_out), .in7(1'b0), .out(ALUSrc), .sel(instr[6:4]));
  Multiplexer #(.select(3), .enable("false")) multiplexer_3 (
    .in0(and_11_out), .in1(1'b0), .in2(1'b0), .in3(1'b0), .in4(1'b0), .in5(1'b0), .in6(1'b0), .in7(1'b0),
    .out(MemRead), .sel(instr[6:4]));
  Multiplexer #(.select(3), .enable("false")) multiplexer_4 (
    .in0(and_11_out), .in1(1'b0), .in2(1'b0), .in3(1'b0), .in4(1'b0), .in5(1'b0), .in6(1'b0), .in7(1'b0),
    .out(MemToReg), .sel(instr[6:4]));
  Multiplexer #(.select(3), .enable("false")) multiplexer_5 (
    .in0(1'b0), .in1(1'b0), .in2(and_12_out), .in3(1'b0), .in4(1'b0), .in5(1'b0), .in6(1'b0), .in7(1'b0),
    .out(MemWrite), .sel(instr[6:4]));
  Multiplexer #(.select(3), .enable("false")) multiplexer_6 (
    .in0(1'b0), .in1(1'b0), .in2(1'b0), .in3(1'b0), .in4(1'b0), .in5(1'b0), .in6(and_13_out), .in7(1'b0),
    .out(PCSrc), .sel(instr[6:4]));
  Multiplexer #(.select(3), .enable("false")) multiplexer_7 (
    .in0(1'b0), .in1(1'b0), .in2(1'b0), .in3(1'b0), .in4(1'b0), .in5(1'b0), .in6(and_14_out), .in7(1'b0),
    .out(Jump), .sel(instr[6:4]));
  or or_1 (ALUOp[0], instr[30], instr[25]);

  assign ALUOp[3:1] = instr[14:12];

  // Other names for the same wires on the sheet: funct3[2:0] = instr[14:12]; OpCode2[3:0] = instr[3:0];
  //   OpCode1[2:0] = instr[6:4]; funct7[6:0] = instr[31:25]

  // Notes on the sheet:
  //   Entradas
  //   Datapath
  //   Salidas
  //   Type-R
  //   Type-I
  //   Load
  //   Store
  //   Branch
  //   JAL
endmodule
