// Logisim project Instruction Fetch.circ as structural Verilog: 1 circuit, main circuit main
module main (
);

  wire clock_1_out;
  wire [31:0] adder_1_out, counter_1_q, Instruction_Memory_data, multiplexer_1_out, register_2_q;

  Multiplexer #(.width(32), .enable("false")) multiplexer_1 (
    .in0(adder_1_out), .out(multiplexer_1_out), .sel(1'b0));  // open: in1
  Counter #(.width(32), .max('hffffffff)) counter_1 (
    .D(multiplexer_1_out), .Q(counter_1_q), .clk(clock_1_out));  // open: load, count, carry, clr, preset, down
  Clock clock_1 (.out(clock_1_out));
  Adder #(.width(32)) adder_1 (.a(32'h4), .b(counter_1_q), .out(adder_1_out));  // open: cin, cout
  ROM #(.dataWidth(32), .Select("low")) Instruction_Memory (.addr(counter_1_q[9:2]), .data(Instruction_Memory_data));
  Register #(.width(32), .Select("low")) register_1 (.D(counter_1_q));  // open: en, Q, clk, clr
  Register #(.width(32), .Select("low")) register_2 (
    .D(Instruction_Memory_data), .Q(register_2_q));  // open: en, clk, clr

  // Notes on the sheet:
  //   R-type
  //   I-type
  //   S-type
endmodule
