// Logisim project Pipelining_RISC_V_CPU_ForwardingAndHazardDetectionUnits.circ as structural Verilog: 12 circuits, main circuit main
module main (
  input  Clock,
  output out_2
);

  wire alu_1_greater_than_zero, alu_1_less_than_zero, alu_1_zero, and_1_out, control_unit_1_memread,
       control_unit_1_memtoreg, control_unit_1_memwrite, control_unit_1_pcsrc, control_unit_1_regwrite,
       control_unit_1_signedop, ex_mem_1_mem_greaterthan, ex_mem_1_mem_greaterthan_2, ex_mem_1_mem_zero,
       ex_mem_1_memread_2, ex_mem_1_memtoreg_2, ex_mem_1_memwrite_2, ex_mem_1_regwrite_2,
       Forwarding_Unit_fw_01, Forwarding_Unit_fw_10, ID_EX_memread_2, ID_EX_memtoreg_2, ID_EX_memwrite_2,
       ID_EX_pcsrc_2, ID_EX_regwrite_2, mem_wb_1_memtoreg_2, mem_wb_1_regwrite_2, multiplexer_7_out, NE_out,
       not_1_out, or_1_out, undriven;
  wire [1:0] control_unit_1_alusrc, control_unit_1_branchcode, ex_mem_1_branchcode_2, ID_EX_alusrc_2,
       ID_EX_branchcode_2;
  wire [3:0] control_unit_1_aluop, ID_EX_aluop_2;
  wire [4:0] ex_mem_1_mem_writeregister, ID_EX_id_writeregister, IF_ID_id_instr_2, IF_ID_id_instr_3,
       mem_wb_1_writeregister_2;
  wire [31:0] adder_1_out, adder_2_out, alu_1_aluresult, bit_extender_1_out, bit_extender_2_out,
       bit_extender_3_out, bit_extender_4_out, counter_1_q, ex_mem_1_mem_aluresult, ex_mem_1_mem_pc_4,
       ID_EX_id_imm_branch, ID_EX_id_imm_jump, ID_EX_id_imm_lw_xl, ID_EX_id_imm_sw, ID_EX_id_pc_4,
       ID_EX_id_rs1, ID_EX_id_rs2, IF_ID_id_instr, IF_ID_id_pc_4, Instruction_Memory_data,
       mem_wb_1_wb_aluresult, mem_wb_1_wb_readdata, memory_1_readdata, multiplexer_1_out, multiplexer_2_out,
       multiplexer_3_out, multiplexer_4_out, multiplexer_5_out, multiplexer_6_out, multiplexer_8_out,
       register_file_1_d1, register_file_1_d2;

  Multiplexer #(.width(32), .enable("false")) multiplexer_1 (
    .in0(adder_1_out), .in1(multiplexer_2_out), .out(multiplexer_1_out), .sel(or_1_out));
  buf or_1 (or_1_out, control_unit_1_signedop);  // OR_Gate
  Counter #(.width(32), .max('hffffffff)) counter_1 (
    .D(multiplexer_1_out), .Q(counter_1_q), .clk(Clock), .clr(undriven));  // open: load, count, carry, preset, down
  Adder #(.width(32)) adder_1 (.a(32'h4), .b(counter_1_q), .out(adder_1_out));  // open: cin, cout
  ROM #(.dataWidth(32), .Select("low")) Instruction_Memory (.addr(counter_1_q[9:2]), .data(Instruction_Memory_data));
  Hazard_Detection_Unit hazard_detection_unit_1 (
    .ID_EX_MemRead(ID_EX_memread_2), .ID_EX_RegisterRT(ID_EX_id_rs2[19:15]),
    .IF_ID_RegisterRT(IF_ID_id_instr_3), .IF_ID_RegisterRS(IF_ID_id_instr_2), .Stall(out_2));
  IF_ID IF_ID (
    .IF_PC_4(adder_1_out), .Clock(Clock), .IF_Instr(Instruction_Memory_data), .ID_PC_4(IF_ID_id_pc_4),
    .ID_Instr({IF_ID_id_instr[31:25], IF_ID_id_instr_2, IF_ID_id_instr_3, IF_ID_id_instr[14:0]}));
  Control_Unit control_unit_1 (
    .Instr({IF_ID_id_instr[31:25], IF_ID_id_instr_2, IF_ID_id_instr_3, IF_ID_id_instr[14:0]}),
    .ALUOp(control_unit_1_aluop), .ALUSrc(control_unit_1_alusrc), .SignedOp(control_unit_1_signedop),
    .BranchCode(control_unit_1_branchcode), .PCSrc(control_unit_1_pcsrc), .MemRead(control_unit_1_memread),
    .MemWrite(control_unit_1_memwrite), .MemToReg(control_unit_1_memtoreg), .RegWrite(control_unit_1_regwrite));
  Register_File register_file_1 (
    .write_data(multiplexer_8_out), .rs1(IF_ID_id_instr_2), .rs2(IF_ID_id_instr_3),
    .in_1(mem_wb_1_regwrite_2), .d1(register_file_1_d1), .write_register(mem_wb_1_writeregister_2),
    .d2(register_file_1_d2), .Clock(Clock));
  assign bit_extender_1_out = {{20{IF_ID_id_instr[31]}}, {IF_ID_id_instr[31:25], IF_ID_id_instr_2}};  // Bit_Extender bit_extender_1
  assign bit_extender_2_out = {{20{IF_ID_id_instr[31]}}, {IF_ID_id_instr[31:25], IF_ID_id_instr[11:7]}};  // Bit_Extender bit_extender_2
  assign bit_extender_3_out = {{11{IF_ID_id_instr[31]}}, {IF_ID_id_instr[31], IF_ID_id_instr_3, IF_ID_id_instr[14:12], IF_ID_id_instr_2[0], IF_ID_id_instr[30:25], IF_ID_id_instr_2[4:1], 1'b0}};  // Bit_Extender bit_extender_3
  assign bit_extender_4_out = {{19{IF_ID_id_instr[31]}}, {IF_ID_id_instr[31], IF_ID_id_instr[7], IF_ID_id_instr[30:25], IF_ID_id_instr[11:8], 1'b0}};  // Bit_Extender bit_extender_4
  Multiplexer #(.width(32), .enable("false")) multiplexer_2 (
    .in0(ex_mem_1_mem_pc_4), .in1(adder_2_out), .out(multiplexer_2_out), .sel(and_1_out));
  ID_EX ID_EX (
    .Clock(Clock), .IF_PC_4(IF_ID_id_pc_4), .IF_rs1(register_file_1_d1), .IF_rs2(register_file_1_d2),
    .IF_WriteRegister(IF_ID_id_instr[11:7]), .IF_Imm_LW_xl(bit_extender_1_out),
    .IF_Imm_SW(bit_extender_2_out), .IF_Imm_Branch(bit_extender_3_out), .IF_Imm_Jump(bit_extender_4_out),
    .ID_PC_4(ID_EX_id_pc_4), .ID_rs1(ID_EX_id_rs1), .ID_rs2(ID_EX_id_rs2),
    .ID_WriteRegister(ID_EX_id_writeregister), .ID_Imm_LW_xl(ID_EX_id_imm_lw_xl),
    .ID_Imm_SW(ID_EX_id_imm_sw), .ID_Imm_Branch(ID_EX_id_imm_branch), .ID_Imm_Jump(ID_EX_id_imm_jump),
    .ALUOp(control_unit_1_aluop), .ALUOp_2(ID_EX_aluop_2), .ALUSrc(control_unit_1_alusrc),
    .ALUSrc_2(ID_EX_alusrc_2), .SignedOp(control_unit_1_signedop), .SignedOp_2(control_unit_1_signedop),
    .BranchCode(control_unit_1_branchcode), .BranchCode_2(ID_EX_branchcode_2), .PCSrc(control_unit_1_pcsrc),
    .PCSrc_2(ID_EX_pcsrc_2), .MemRead(control_unit_1_memread), .MemRead_2(ID_EX_memread_2),
    .MemWrite(control_unit_1_memwrite), .MemWrite_2(ID_EX_memwrite_2), .MemToReg(control_unit_1_memtoreg),
    .MemToReg_2(ID_EX_memtoreg_2), .RegWrite(control_unit_1_regwrite), .RegWrite_2(ID_EX_regwrite_2));
  Multiplexer #(.width(32), .enable("false")) multiplexer_3 (
    .in0(ID_EX_id_imm_branch), .in1(ID_EX_id_imm_jump), .out(multiplexer_3_out), .sel(ID_EX_pcsrc_2));
  and and_1 (and_1_out, multiplexer_7_out, not_1_out);
  not not_1 (not_1_out, ID_EX_pcsrc_2);
  Multiplexer #(.width(32), .enable("false")) multiplexer_4 (
    .in0(multiplexer_5_out), .in1(multiplexer_8_out), .out(multiplexer_4_out), .sel(Forwarding_Unit_fw_10));
  Multiplexer #(.select(2), .width(32), .enable("false")) multiplexer_5 (
    .in0(ID_EX_id_rs2), .in1(ID_EX_id_imm_lw_xl), .in2(ID_EX_id_imm_sw), .out(multiplexer_5_out),
    .sel(ID_EX_alusrc_2));  // open: in3
  Forwarding_Unit Forwarding_Unit (
    .ID_EX_RegisterRs(ID_EX_id_rs1[24:20]), .ID_EX_RegisterRt(ID_EX_id_rs2[19:15]),
    .EX_MEM_RegisterRd(ex_mem_1_mem_writeregister), .EX_MEM_RegWrite(ex_mem_1_regwrite_2),
    .MEM_WB_RegisterRd(mem_wb_1_writeregister_2), .MEM_WB_RegWrite(mem_wb_1_regwrite_2),
    .FW_01(Forwarding_Unit_fw_01), .FW_10(Forwarding_Unit_fw_10));
  Multiplexer #(.width(32), .enable("false")) multiplexer_6 (
    .in0(ID_EX_id_rs1), .in1(multiplexer_8_out), .out(multiplexer_6_out), .sel(Forwarding_Unit_fw_01));
  ALU alu_1 (
    .ALUResult(alu_1_aluresult), .A(multiplexer_6_out), .B(multiplexer_4_out), .ALUOp(ID_EX_aluop_2),
    .Greater_than_zero(alu_1_greater_than_zero), .Zero(alu_1_zero), .Less_than_zero(alu_1_less_than_zero));  // open: SignedCmp
  EX_MEM ex_mem_1 (
    .Clock(Clock), .EX_PC_4(adder_2_out), .EX_ALUResult(alu_1_aluresult),
    .EX_WriteRegister(ID_EX_id_writeregister), .EX_Zero(alu_1_zero),
    .EX_GreaterThan(alu_1_greater_than_zero), .EX_LessThan(alu_1_less_than_zero),
    .MEM_PC_4(ex_mem_1_mem_pc_4), .MEM_ALUResult(ex_mem_1_mem_aluresult),
    .MEM_WriteRegister(ex_mem_1_mem_writeregister), .MEM_Zero(ex_mem_1_mem_zero),
    .MEM_GreaterThan(ex_mem_1_mem_greaterthan), .MEM_GreaterThan_2(ex_mem_1_mem_greaterthan_2),
    .BranchCode(ID_EX_branchcode_2), .BranchCode_2(ex_mem_1_branchcode_2), .MemRead(ID_EX_memread_2),
    .MemRead_2(ex_mem_1_memread_2), .MemWrite(ID_EX_memwrite_2), .MemWrite_2(ex_mem_1_memwrite_2),
    .MemToReg(ID_EX_memtoreg_2), .MemToReg_2(ex_mem_1_memtoreg_2), .RegWrite(ID_EX_regwrite_2),
    .RegWrite_2(ex_mem_1_regwrite_2));
  Adder #(.width(32)) adder_2 (.a(ID_EX_id_pc_4), .b(multiplexer_3_out), .out(adder_2_out));  // open: cin, cout
  or GE (ex_mem_1_regwrite_2, ex_mem_1_mem_zero, ex_mem_1_mem_greaterthan);
  or NE (NE_out, ex_mem_1_mem_greaterthan, ex_mem_1_mem_greaterthan_2);
  Multiplexer #(.select(2), .enable("false")) multiplexer_7 (
    .in0(ex_mem_1_mem_zero), .in1(NE_out), .in2(ex_mem_1_mem_greaterthan_2), .in3(ex_mem_1_regwrite_2),
    .out(multiplexer_7_out), .sel(ex_mem_1_branchcode_2));
  Memory memory_1 (
    .Address(ex_mem_1_mem_aluresult), .MemWrite(ex_mem_1_memwrite_2), .Clock(Clock),
    .MemRead(ex_mem_1_memread_2), .ReadData(memory_1_readdata));  // open: WriteData
  MEM_WB mem_wb_1 (
    .MEM_ALUResult(ex_mem_1_mem_aluresult), .Clock(Clock), .MEM_ReadData(memory_1_readdata),
    .WB_ALUResult(mem_wb_1_wb_aluresult), .WB_ReadData(mem_wb_1_wb_readdata), .RegWrite(ex_mem_1_regwrite_2),
    .MemToReg(ex_mem_1_memtoreg_2), .RegWrite_2(mem_wb_1_regwrite_2), .MemToReg_2(mem_wb_1_memtoreg_2),
    .WriteRegister(ex_mem_1_mem_writeregister), .WriteRegister_2(mem_wb_1_writeregister_2));
  Multiplexer #(.width(32), .enable("false")) multiplexer_8 (
    .in0(mem_wb_1_wb_aluresult), .in1(mem_wb_1_wb_readdata), .out(multiplexer_8_out),
    .sel(mem_wb_1_memtoreg_2));

  // Notes on the sheet:
  //   contents of Instruction_Memory (hex, n*v repeats v):
  //   211020 a21820 462020 842820 ac850080
  //   R-type
  //   SW
  //   Jump
  //   Branch
endmodule

module ALU (
  input  [31:0] A,
  input  [31:0] B,
  input  [3:0] ALUOp,
  output Greater_than_zero,
  output Zero,
  output Less_than_zero,
  output SignedCmp,
  output [31:0] ALUResult
);

  wire comparator_1_lt, comparator_2_lt, comparator_3_eq, comparator_3_gt, comparator_3_lt, comparator_4_eq,
       comparator_4_gt, comparator_4_lt;
  wire [31:0] adder_1_out, and_1_out, bit_extender_1_out, bit_extender_2_out, divider_1_out,
       multiplier_1_out, nand_1_out, negator_1_out, nor_1_out, not_1_out, or_1_out, shifter_1_out,
       shifter_2_out, shifter_3_out, subtractor_1_out, xor_1_out;

  Adder #(.width(32)) adder_1 (.a(A), .b(B), .out(adder_1_out));  // open: cin, cout
  Subtractor #(.width(32)) subtractor_1 (.a(A), .b(B), .out(subtractor_1_out));  // open: bin, bout
  Multiplier #(.width(32)) multiplier_1 (.a(A), .b(B), .out(multiplier_1_out));  // open: cin, cout
  Divider #(.width(32)) divider_1 (.a(A), .b(B), .out(divider_1_out));  // open: upper, rem
  assign and_1_out = A & B;  // AND_Gate and_1, 32 bits wide
  assign nand_1_out = ~(A & B);  // NAND_Gate nand_1, 32 bits wide
  assign nor_1_out = ~(A | B);  // NOR_Gate nor_1, 32 bits wide
  assign not_1_out = ~A;  // NOT_Gate not_1, 32 bits wide
  assign or_1_out = A | B;  // OR_Gate or_1, 32 bits wide
  assign xor_1_out = A ^ B;  // XOR_Gate xor_1, 32 bits wide
  Shifter #(.width(32)) shifter_1 (.in(A), .\dist (B[4:0]), .out(shifter_1_out));
  Shifter #(.width(32), .shift("lr")) shifter_2 (.in(A), .\dist (B[4:0]), .out(shifter_2_out));
  Shifter #(.width(32), .shift("ar")) shifter_3 (.in(A), .\dist (B[4:0]), .out(shifter_3_out));
  Comparator #(.width(32)) comparator_1 (.a(A), .b(B), .lt(comparator_1_lt));  // open: gt, eq
  Comparator #(.width(32), .mode("unsigned")) comparator_2 (.a(A), .b(B), .lt(comparator_2_lt));  // open: gt, eq
  Negator #(.width(32)) negator_1 (.in(A), .out(negator_1_out));
  assign bit_extender_1_out = {{31{1'b0}}, comparator_1_lt};  // Bit_Extender bit_extender_1
  assign bit_extender_2_out = {{31{1'b0}}, comparator_2_lt};  // Bit_Extender bit_extender_2
  Multiplexer #(.select(4), .width(32), .enable("false")) multiplexer_1 (
    .in0(adder_1_out), .in1(subtractor_1_out), .in2(multiplier_1_out), .in3(divider_1_out), .in4(and_1_out),
    .in5(nand_1_out), .in6(nor_1_out), .in7(not_1_out), .in8(or_1_out), .in9(xor_1_out),
    .in10(shifter_1_out), .in11(shifter_2_out), .in12(shifter_3_out), .in13(bit_extender_1_out),
    .in14(bit_extender_2_out), .in15(negator_1_out), .out(ALUResult), .sel(ALUOp));
  Comparator #(.width(32)) comparator_3 (
    .a(ALUResult), .b({32{1'b0}}), .gt(comparator_3_gt), .eq(comparator_3_eq), .lt(comparator_3_lt));
  Comparator #(.width(32)) comparator_4 (
    .a(ALUResult), .b({32{1'b0}}), .gt(comparator_4_gt), .eq(comparator_4_eq), .lt(comparator_4_lt));
  Multiplexer #(.enable("false")) multiplexer_2 (
    .in0(comparator_3_gt), .in1(comparator_4_gt), .out(Greater_than_zero), .sel(SignedCmp));
  Multiplexer #(.enable("false")) multiplexer_3 (
    .in0(comparator_3_eq), .in1(comparator_4_eq), .out(Zero), .sel(SignedCmp));
  Multiplexer #(.enable("false")) multiplexer_4 (
    .in0(comparator_3_lt), .in1(comparator_4_lt), .out(Less_than_zero), .sel(SignedCmp));
endmodule

module Register_File (
  input  in_1,
  input  [4:0] rs1,
  input  [31:0] write_data,
  input  [4:0] write_register,
  input  [4:0] rs2,
  input  Clock,
  output [31:0] d1,
  output [31:0] d2
);

  wire demultiplexer_2_out0, demultiplexer_2_out1, demultiplexer_2_out2, demultiplexer_2_out3,
       demultiplexer_2_out4, demultiplexer_2_out5, demultiplexer_2_out6, demultiplexer_2_out7,
       demultiplexer_2_out8, demultiplexer_2_out9, demultiplexer_2_out10, demultiplexer_2_out11,
       demultiplexer_2_out12, demultiplexer_2_out13, demultiplexer_2_out14, demultiplexer_2_out15,
       demultiplexer_2_out16, demultiplexer_2_out17, demultiplexer_2_out18, demultiplexer_2_out19,
       demultiplexer_2_out20, demultiplexer_2_out21, demultiplexer_2_out22, demultiplexer_2_out23,
       demultiplexer_2_out24, demultiplexer_2_out25, demultiplexer_2_out26, demultiplexer_2_out27,
       demultiplexer_2_out28, demultiplexer_2_out29, demultiplexer_2_out30, demultiplexer_2_out31;
  wire [31:0] demultiplexer_1_out1, demultiplexer_1_out2, demultiplexer_1_out3, demultiplexer_1_out4,
       demultiplexer_1_out5, demultiplexer_1_out6, demultiplexer_1_out7, demultiplexer_1_out8,
       demultiplexer_1_out9, demultiplexer_1_out10, demultiplexer_1_out11, demultiplexer_1_out12,
       demultiplexer_1_out13, demultiplexer_1_out14, demultiplexer_1_out15, demultiplexer_1_out16,
       demultiplexer_1_out17, demultiplexer_1_out18, demultiplexer_1_out19, demultiplexer_1_out20,
       demultiplexer_1_out21, demultiplexer_1_out22, demultiplexer_1_out23, demultiplexer_1_out24,
       demultiplexer_1_out25, demultiplexer_1_out26, demultiplexer_1_out27, demultiplexer_1_out28,
       demultiplexer_1_out29, demultiplexer_1_out30, demultiplexer_1_out31, R1_q, R2_q, R3_q, R4_q, R5_q,
       R6_q, R7_q, R8_q, R9_q, R10_q, R11_q, R12_q, R13_q, R14_q, R15_q, R16_q, R17_q, R18_q, R19_q, R20_q,
       R21_q, R22_q, R23_q, R24_q, R25_q, R26_q, R27_q, R28_q, R29_q, R30_q, R31_q;

  Demultiplexer #(.select(5), .width(32), .enable("false")) demultiplexer_1 (
    .out1(demultiplexer_1_out1), .out2(demultiplexer_1_out2), .out3(demultiplexer_1_out3),
    .out4(demultiplexer_1_out4), .out5(demultiplexer_1_out5), .out6(demultiplexer_1_out6),
    .out7(demultiplexer_1_out7), .out8(demultiplexer_1_out8), .out9(demultiplexer_1_out9),
    .out10(demultiplexer_1_out10), .out11(demultiplexer_1_out11), .out12(demultiplexer_1_out12),
    .out13(demultiplexer_1_out13), .out14(demultiplexer_1_out14), .out15(demultiplexer_1_out15),
    .out16(demultiplexer_1_out16), .out17(demultiplexer_1_out17), .out18(demultiplexer_1_out18),
    .out19(demultiplexer_1_out19), .out20(demultiplexer_1_out20), .out21(demultiplexer_1_out21),
    .out22(demultiplexer_1_out22), .out23(demultiplexer_1_out23), .out24(demultiplexer_1_out24),
    .out25(demultiplexer_1_out25), .out26(demultiplexer_1_out26), .out27(demultiplexer_1_out27),
    .out28(demultiplexer_1_out28), .out29(demultiplexer_1_out29), .out30(demultiplexer_1_out30),
    .out31(demultiplexer_1_out31), .in(write_data), .sel(write_register));  // open: out0
  Register #(.width(32), .Select("low")) R8 (
    .D(demultiplexer_1_out15), .en(demultiplexer_2_out8), .Q(R8_q), .clk(Clock));  // open: clr
  Register #(.width(32), .Select("low")) R1 (
    .D(demultiplexer_1_out1), .en(demultiplexer_2_out1), .Q(R1_q), .clk(Clock));  // open: clr
  Register #(.width(32), .Select("low")) R9 (
    .D(demultiplexer_1_out14), .en(demultiplexer_2_out9), .Q(R9_q), .clk(Clock));  // open: clr
  Register #(.width(32), .Select("low")) R2 (
    .D(demultiplexer_1_out2), .en(demultiplexer_2_out2), .Q(R2_q), .clk(Clock));  // open: clr
  Register #(.width(32), .Select("low")) R10 (
    .D(demultiplexer_1_out13), .en(demultiplexer_2_out10), .Q(R10_q), .clk(Clock));  // open: clr
  Register #(.width(32), .Select("low")) R3 (
    .D(demultiplexer_1_out3), .en(demultiplexer_2_out3), .Q(R3_q), .clk(Clock));  // open: clr
  Register #(.width(32), .Select("low")) R11 (
    .D(demultiplexer_1_out12), .en(demultiplexer_2_out11), .Q(R11_q), .clk(Clock));  // open: clr
  Register #(.width(32), .Select("low")) R4 (
    .D(demultiplexer_1_out4), .en(demultiplexer_2_out4), .Q(R4_q), .clk(Clock));  // open: clr
  Register #(.width(32), .Select("low")) R12 (
    .D(demultiplexer_1_out11), .en(demultiplexer_2_out12), .Q(R12_q), .clk(Clock));  // open: clr
  Register #(.width(32), .Select("low")) R5 (
    .D(demultiplexer_1_out5), .en(demultiplexer_2_out5), .Q(R5_q), .clk(Clock));  // open: clr
  Register #(.width(32), .Select("low")) R13 (
    .D(demultiplexer_1_out10), .en(demultiplexer_2_out13), .Q(R13_q), .clk(Clock));  // open: clr
  Register #(.width(32), .Select("low")) R6 (
    .D(demultiplexer_1_out6), .en(demultiplexer_2_out6), .Q(R6_q), .clk(Clock));  // open: clr
  Register #(.width(32), .Select("low")) R7 (
    .D(demultiplexer_1_out7), .en(demultiplexer_2_out7), .Q(R7_q), .clk(Clock));  // open: clr
  Register #(.width(32), .Select("low")) R14 (
    .D(demultiplexer_1_out9), .en(demultiplexer_2_out14), .Q(R14_q), .clk(Clock));  // open: clr
  Register #(.width(32), .Select("low")) R15 (
    .D(demultiplexer_1_out8), .en(demultiplexer_2_out15), .Q(R15_q), .clk(Clock));  // open: clr
  Demultiplexer #(.select(5), .enable("false")) demultiplexer_2 (
    .out0(demultiplexer_2_out0), .out1(demultiplexer_2_out1), .out2(demultiplexer_2_out2),
    .out3(demultiplexer_2_out3), .out4(demultiplexer_2_out4), .out5(demultiplexer_2_out5),
    .out6(demultiplexer_2_out6), .out7(demultiplexer_2_out7), .out8(demultiplexer_2_out8),
    .out9(demultiplexer_2_out9), .out10(demultiplexer_2_out10), .out11(demultiplexer_2_out11),
    .out12(demultiplexer_2_out12), .out13(demultiplexer_2_out13), .out14(demultiplexer_2_out14),
    .out15(demultiplexer_2_out15), .out16(demultiplexer_2_out16), .out17(demultiplexer_2_out17),
    .out18(demultiplexer_2_out18), .out19(demultiplexer_2_out19), .out20(demultiplexer_2_out20),
    .out21(demultiplexer_2_out21), .out22(demultiplexer_2_out22), .out23(demultiplexer_2_out23),
    .out24(demultiplexer_2_out24), .out25(demultiplexer_2_out25), .out26(demultiplexer_2_out26),
    .out27(demultiplexer_2_out27), .out28(demultiplexer_2_out28), .out29(demultiplexer_2_out29),
    .out30(demultiplexer_2_out30), .out31(demultiplexer_2_out31), .in(in_1), .sel(write_register));
  Multiplexer #(.select(5), .enable("false")) multiplexer_1 (
    .in0(demultiplexer_2_out0), .in1(demultiplexer_2_out1), .in2(demultiplexer_2_out2),
    .in3(demultiplexer_2_out3), .in4(demultiplexer_2_out4), .in5(demultiplexer_2_out5),
    .in6(demultiplexer_2_out6), .in7(demultiplexer_2_out7), .in8(demultiplexer_2_out8),
    .in9(demultiplexer_2_out9), .in10(demultiplexer_2_out10), .in11(demultiplexer_2_out11),
    .in12(demultiplexer_2_out12), .in13(demultiplexer_2_out13), .in14(demultiplexer_2_out14),
    .in15(demultiplexer_2_out15), .in16(demultiplexer_2_out16), .in17(demultiplexer_2_out17),
    .in18(demultiplexer_2_out18), .in19(demultiplexer_2_out19), .in20(demultiplexer_2_out20),
    .in21(demultiplexer_2_out21), .in22(demultiplexer_2_out22), .in23(demultiplexer_2_out23),
    .in24(demultiplexer_2_out24), .in25(demultiplexer_2_out25), .in26(demultiplexer_2_out26),
    .in27(demultiplexer_2_out27), .in28(demultiplexer_2_out28), .in29(demultiplexer_2_out29),
    .in30(demultiplexer_2_out30), .in31(demultiplexer_2_out31));  // open: out, sel
  Multiplexer #(.select(5), .width(32), .enable("false")) multiplexer_2 (
    .in0({32{1'b0}}), .in1(R1_q), .in2(R2_q), .in3(R3_q), .in4(R4_q), .in5(R5_q), .in6(R6_q), .in7(R7_q),
    .in8(R15_q), .in9(R14_q), .in10(R13_q), .in11(R12_q), .in12(R11_q), .in13(R10_q), .in14(R9_q),
    .in15(R8_q), .in16(R16_q), .in17(R17_q), .in18(R18_q), .in19(R19_q), .in20(R20_q), .in21(R21_q),
    .in22(R22_q), .in23(R23_q), .in24(R24_q), .in25(R25_q), .in26(R26_q), .in27(R27_q), .in28(R28_q),
    .in29(R29_q), .in30(R30_q), .in31(R31_q), .out(d1), .sel(rs1));
  Multiplexer #(.select(5), .width(32), .enable("false")) multiplexer_3 (
    .in0({32{1'b0}}), .in1(R1_q), .in2(R2_q), .in3(R3_q), .in4(R4_q), .in5(R5_q), .in6(R6_q), .in7(R7_q),
    .in8(R15_q), .in9(R14_q), .in10(R13_q), .in11(R12_q), .in12(R11_q), .in13(R10_q), .in14(R9_q),
    .in15(R8_q), .in16(R16_q), .in17(R17_q), .in18(R18_q), .in19(R19_q), .in20(R20_q), .in21(R21_q),
    .in22(R22_q), .in23(R23_q), .in24(R24_q), .in25(R25_q), .in26(R26_q), .in27(R27_q), .in28(R28_q),
    .in29(R29_q), .in30(R30_q), .in31(R31_q), .out(d2), .sel(rs2));
  Register #(.width(32), .Select("low")) R16 (
    .D(demultiplexer_1_out24), .en(demultiplexer_2_out16), .Q(R16_q), .clk(Clock));  // open: clr
  Register #(.width(32), .Select("low")) R24 (
    .D(demultiplexer_1_out23), .en(demultiplexer_2_out24), .Q(R24_q), .clk(Clock));  // open: clr
  Register #(.width(32), .Select("low")) R17 (
    .D(demultiplexer_1_out25), .en(demultiplexer_2_out17), .Q(R17_q), .clk(Clock));  // open: clr
  Register #(.width(32), .Select("low")) R25 (
    .D(demultiplexer_1_out22), .en(demultiplexer_2_out25), .Q(R25_q), .clk(Clock));  // open: clr
  Register #(.width(32), .Select("low")) R18 (
    .D(demultiplexer_1_out26), .en(demultiplexer_2_out18), .Q(R18_q), .clk(Clock));  // open: clr
  Register #(.width(32), .Select("low")) R26 (
    .D(demultiplexer_1_out21), .en(demultiplexer_2_out26), .Q(R26_q), .clk(Clock));  // open: clr
  Register #(.width(32), .Select("low")) R19 (
    .D(demultiplexer_1_out27), .en(demultiplexer_2_out19), .Q(R19_q), .clk(Clock));  // open: clr
  Register #(.width(32), .Select("low")) R20 (
    .D(demultiplexer_1_out28), .en(demultiplexer_2_out20), .Q(R20_q), .clk(Clock));  // open: clr
  Register #(.width(32), .Select("low")) R27 (
    .D(demultiplexer_1_out20), .en(demultiplexer_2_out27), .Q(R27_q));  // open: clk, clr
  Register #(.width(32), .Select("low")) R28 (
    .D(demultiplexer_1_out19), .en(demultiplexer_2_out28), .Q(R28_q), .clk(Clock));  // open: clr
  Register #(.width(32), .Select("low")) R21 (
    .D(demultiplexer_1_out29), .en(demultiplexer_2_out21), .Q(R21_q), .clk(Clock));  // open: clr
  Register #(.width(32), .Select("low")) R29 (
    .D(demultiplexer_1_out18), .en(demultiplexer_2_out29), .Q(R29_q), .clk(Clock));  // open: clr
  Register #(.width(32), .Select("low")) R22 (
    .D(demultiplexer_1_out30), .en(demultiplexer_2_out22), .Q(R22_q), .clk(Clock));  // open: clr
  Register #(.width(32), .Select("low")) R30 (
    .D(demultiplexer_1_out17), .en(demultiplexer_2_out30), .Q(R30_q), .clk(Clock));  // open: clr
  Register #(.width(32), .Select("low")) R23 (
    .D(demultiplexer_1_out31), .en(demultiplexer_2_out23), .Q(R23_q), .clk(Clock));  // open: clr
  Register #(.width(32), .Select("low")) R31 (
    .D(demultiplexer_1_out16), .en(demultiplexer_2_out31), .Q(R31_q), .clk(Clock));  // open: clr
endmodule

module IF_ID (
  input  [31:0] IF_PC_4,
  input  Clock,
  input  [31:0] IF_Instr,
  output [31:0] ID_PC_4,
  output [31:0] ID_Instr
);

  Register #(.width(32), .Select("low")) PC_4 (.D(IF_PC_4), .Q(ID_PC_4), .clk(Clock));  // open: en, clr
  Register #(.width(32), .Select("low")) Instr (.D(IF_Instr), .Q(ID_Instr), .clk(Clock));  // open: en, clr
endmodule

module ID_EX (
  input  Clock,
  input  [31:0] IF_PC_4,
  input  [31:0] IF_rs1,
  input  [31:0] IF_rs2,
  input  [4:0] IF_WriteRegister,
  input  [31:0] IF_Imm_LW_xl,
  input  [31:0] IF_Imm_SW,
  input  [31:0] IF_Imm_Branch,
  input  [31:0] IF_Imm_Jump,
  input  [3:0] ALUOp,
  input  [1:0] ALUSrc,
  input  SignedOp,
  input  [1:0] BranchCode,
  input  PCSrc,
  input  MemRead,
  input  MemWrite,
  input  MemToReg,
  input  RegWrite,
  output [31:0] ID_PC_4,
  output [31:0] ID_rs1,
  output [31:0] ID_rs2,
  output [4:0] ID_WriteRegister,
  output [31:0] ID_Imm_LW_xl,
  output [31:0] ID_Imm_SW,
  output [31:0] ID_Imm_Branch,
  output [31:0] ID_Imm_Jump,
  output [3:0] ALUOp_2,
  output [1:0] ALUSrc_2,
  output SignedOp_2,
  output [1:0] BranchCode_2,
  output PCSrc_2,
  output MemRead_2,
  output MemWrite_2,
  output MemToReg_2,
  output RegWrite_2
);

  Register #(.width(32), .Select("low")) ID_EX_PC_4 (.D(IF_PC_4), .Q(ID_PC_4), .clk(Clock));  // open: en, clr
  Register #(.width(32), .Select("low")) ID_EX_rs1 (.D(IF_rs1), .Q(ID_rs1), .clk(Clock));  // open: en, clr
  Register #(.width(32), .Select("low")) ID_EX_rs2 (.D(IF_rs2), .Q(ID_rs2), .clk(Clock));  // open: en, clr
  Register #(.width(5), .Select("low")) ID_EX_WriteRegister (
    .D(IF_WriteRegister), .Q(ID_WriteRegister), .clk(Clock));  // open: en, clr
  Register #(.width(32), .Select("low")) ID_EX_Imm_LW_xl (
    .D(IF_Imm_LW_xl), .Q(ID_Imm_LW_xl), .clk(Clock));  // open: en, clr
  Register #(.width(32), .Select("low")) ID_EX_Imm_SW (.D(IF_Imm_SW), .Q(ID_Imm_SW), .clk(Clock));  // open: en, clr
  Register #(.width(32), .Select("low")) ID_EX_Imm_Branch (
    .D(IF_Imm_Branch), .Q(ID_Imm_Branch), .clk(Clock));  // open: en, clr
  Register #(.width(32), .Select("low")) ID_EX_Imm_Jump (
    .D(IF_Imm_Jump), .Q(ID_Imm_Jump), .clk(Clock));  // open: en, clr
  Register #(.width(4), .Select("low")) register_1 (.D(ALUOp), .Q(ALUOp_2), .clk(Clock));  // open: en, clr
  Register #(.width(2), .Select("low")) register_2 (.D(ALUSrc), .Q(ALUSrc_2), .clk(Clock));  // open: en, clr
  Register #(.width(1), .Select("low")) register_3 (.D(SignedOp), .Q(SignedOp_2), .clk(Clock));  // open: en, clr
  Register #(.width(2), .Select("low")) register_4 (.D(BranchCode), .Q(BranchCode_2), .clk(Clock));  // open: en, clr
  Register #(.width(1), .Select("low")) register_5 (.D(PCSrc), .Q(PCSrc_2), .clk(Clock));  // open: en, clr
  Register #(.width(1), .Select("low")) register_6 (.D(MemRead), .Q(MemRead_2), .clk(Clock));  // open: en, clr
  Register #(.width(1), .Select("low")) register_7 (.D(MemWrite), .Q(MemWrite_2), .clk(Clock));  // open: en, clr
  Register #(.width(1), .Select("low")) register_8 (.D(MemToReg), .Q(MemToReg_2), .clk(Clock));  // open: en, clr
  Register #(.width(1), .Select("low")) register_9 (.D(RegWrite), .Q(RegWrite_2), .clk(Clock));  // open: en, clr
endmodule

module EX_MEM (
  input  Clock,
  input  [31:0] EX_PC_4,
  input  [31:0] EX_ALUResult,
  input  [4:0] EX_WriteRegister,
  input  EX_Zero,
  input  EX_GreaterThan,
  input  EX_LessThan,
  input  [1:0] BranchCode,
  input  MemRead,
  input  MemWrite,
  input  MemToReg,
  input  RegWrite,
  output [31:0] MEM_PC_4,
  output [31:0] MEM_ALUResult,
  output [4:0] MEM_WriteRegister,
  output MEM_Zero,
  output MEM_GreaterThan,
  output MEM_GreaterThan_2,
  output [1:0] BranchCode_2,
  output MemRead_2,
  output MemWrite_2,
  output MemToReg_2,
  output RegWrite_2
);

  Register #(.width(32), .Select("low")) EX_MEM_PC_4 (.D(EX_PC_4), .Q(MEM_PC_4), .clk(Clock));  // open: en, clr
  Register #(.width(32), .Select("low")) EX_MEM_ALUResult (
    .D(EX_ALUResult), .Q(MEM_ALUResult), .clk(Clock));  // open: en, clr
  Register #(.width(5), .Select("low")) EX_MEM_WriteRegister (
    .D(EX_WriteRegister), .Q(MEM_WriteRegister), .clk(Clock));  // open: en, clr
  Register #(.width(1), .Select("low")) EX_MEM_Zero (.D(EX_Zero), .Q(MEM_Zero), .clk(Clock));  // open: en, clr
  Register #(.width(1), .Select("low")) EX_MEM_GreaterThan (
    .D(EX_GreaterThan), .Q(MEM_GreaterThan), .clk(Clock));  // open: en, clr
  Register #(.width(1), .Select("low")) EX_MEM_GreaterThan_2 (
    .D(EX_LessThan), .Q(MEM_GreaterThan_2), .clk(Clock));  // open: en, clr
  Register #(.width(2), .Select("low")) register_1 (.D(BranchCode), .Q(BranchCode_2), .clk(Clock));  // open: en, clr
  Register #(.width(1), .Select("low")) register_2 (.D(MemRead), .Q(MemRead_2), .clk(Clock));  // open: en, clr
  Register #(.width(1), .Select("low")) register_3 (.D(MemWrite), .Q(MemWrite_2), .clk(Clock));  // open: en, clr
  Register #(.width(1), .Select("low")) register_4 (.D(MemToReg), .Q(MemToReg_2), .clk(Clock));  // open: en, clr
  Register #(.width(1), .Select("low")) register_5 (.D(RegWrite), .Q(RegWrite_2), .clk(Clock));  // open: en, clr
endmodule

module MEM_WB (
  input  [31:0] MEM_ALUResult,
  input  Clock,
  input  [31:0] MEM_ReadData,
  input  RegWrite,
  input  MemToReg,
  input  [4:0] WriteRegister,
  output [31:0] WB_ALUResult,
  output [31:0] WB_ReadData,
  output RegWrite_2,
  output MemToReg_2,
  output [4:0] WriteRegister_2
);

  Register #(.width(32), .Select("low")) MEM_WB_ALUResult (
    .D(MEM_ALUResult), .Q(WB_ALUResult), .clk(Clock));  // open: en, clr
  Register #(.width(32), .Select("low")) MEM_WB_ReadData (
    .D(MEM_ReadData), .Q(WB_ReadData), .clk(Clock));  // open: en, clr
  Register #(.width(1), .Select("low")) register_1 (.D(RegWrite), .Q(RegWrite_2), .clk(Clock));  // open: en, clr
  Register #(.width(1), .Select("low")) register_2 (.D(MemToReg), .Q(MemToReg_2), .clk(Clock));  // open: en, clr
  Register #(.width(5), .Select("low")) register_3 (
    .D(WriteRegister), .Q(WriteRegister_2), .clk(Clock));  // open: en, clr
endmodule

module Control_Unit (
  input  [31:0] Instr,
  output [3:0] ALUOp,
  output [1:0] ALUSrc,
  output SignedOp,
  output [1:0] BranchCode,
  output PCSrc,
  output MemRead,
  output MemWrite,
  output MemToReg,
  output RegWrite
);

  wire Branch, Jump, LB, LH, SB, SH, Type_I, Type_R;

  and and_1 (Type_R, Instr[0], Instr[1], ~Instr[2], ~Instr[3], Instr[4], Instr[5], ~Instr[6]);  // AND_Gate
  and and_2 (Type_I, Instr[0], Instr[1], ~Instr[2], ~Instr[3], Instr[4], ~Instr[5], ~Instr[6]);  // AND_Gate
  and and_3 (MemRead, Instr[0], Instr[1], ~Instr[2], ~Instr[3], ~Instr[4], ~Instr[5], ~Instr[6]);  // AND_Gate
  and and_4 (ALUSrc[1], Instr[0], Instr[1], ~Instr[2], ~Instr[3], ~Instr[4], Instr[5], ~Instr[6]);  // AND_Gate
  and and_5 (Branch, Instr[0], Instr[1], ~Instr[2], ~Instr[3], ~Instr[4], Instr[5], Instr[6]);  // AND_Gate
  and and_6 (Jump, Instr[0], Instr[1], Instr[2], Instr[3], ~Instr[4], Instr[5], Instr[6]);  // AND_Gate
  and and_7 (LB, ~Instr[0], ~Instr[1], ~Instr[2], Instr[3], ~Instr[4], ~Instr[5], Instr[6]);  // AND_Gate
  and and_8 (LH, Instr[0], ~Instr[1], ~Instr[2], Instr[3], ~Instr[4], ~Instr[5], Instr[6]);  // AND_Gate
  and and_9 (SB, ~Instr[0], ~Instr[1], ~Instr[2], Instr[3], Instr[4], ~Instr[5], Instr[6]);  // AND_Gate
  and and_10 (SH, Instr[0], ~Instr[1], ~Instr[2], Instr[3], ~Instr[4], ~Instr[5], Instr[6]);  // AND_Gate
  or or_1 (ALUSrc[0], MemRead, Type_I);
  or or_2 (PCSrc, Branch, Jump);
  or or_3 (MemToReg, MemRead, ALUSrc[1]);
  or or_4 (RegWrite, Type_R, Type_I, MemRead, ALUSrc[1]);

  assign ALUOp = {Instr[14:12], Instr[30]};
  assign BranchCode = {Instr[14], Instr[12]};
  assign MemWrite = ALUSrc[1];
  assign SignedOp = Instr[13];

  // Other names for the same wires on the sheet: func7b1 = Instr[30]; funct7[6:0] = Instr[31:25];
  //   funct3[2:0] = Instr[14:12]; Store = ALUSrc[1]; OpCode[6:0] = Instr[6:0]; Load = MemRead
endmodule

module Memory (
  input  [31:0] Address,
  input  [31:0] WriteData,
  input  MemWrite,
  input  Clock,
  input  MemRead,
  output [31:0] ReadData
);

  RAM #(.dataWidth(32), .bus("separate"), .Select("low")) ram_1 (
    .addr(Address[9:2]), .din(WriteData), .data(ReadData), .str(MemWrite), .clk(Clock), .ld(MemRead));  // open: sel, clr

  // Notes on the sheet:
  //   NOTA: ESTA NO ES LA MEMORIA DEL EXAMEN,
  //   VER EL CIRCUITO: DataMemory
endmodule

module Forwarding_Unit (
  input  [4:0] ID_EX_RegisterRs,
  input  [4:0] ID_EX_RegisterRt,
  input  [4:0] EX_MEM_RegisterRd,
  input  EX_MEM_RegWrite,
  input  [4:0] MEM_WB_RegisterRd,
  input  MEM_WB_RegWrite,
  output FW_01,
  output FW_10
);

  wire and_1_out, and_2_out, and_3_out, and_4_out, and_5_out, and_6_out, comparator_1_eq, comparator_2_eq,
       comparator_3_eq, comparator_4_eq, comparator_5_eq, comparator_6_eq, not_1_out, not_2_out;

  Comparator #(.width(5)) comparator_1 (.a(EX_MEM_RegisterRd), .b({5{1'b0}}), .eq(comparator_1_eq));  // open: gt, lt
  Comparator #(.width(5)) comparator_2 (.a(MEM_WB_RegisterRd), .b({5{1'b0}}), .eq(comparator_2_eq));  // open: gt, lt
  not not_1 (not_1_out, comparator_1_eq);
  and and_1 (and_1_out, not_1_out, EX_MEM_RegWrite);
  not not_2 (not_2_out, comparator_2_eq);
  and and_2 (and_2_out, not_2_out, MEM_WB_RegWrite);
  Comparator #(.width(5)) comparator_3 (
    .a(ID_EX_RegisterRs), .b(EX_MEM_RegisterRd), .eq(comparator_3_eq));  // open: gt, lt
  Comparator #(.width(5)) comparator_4 (
    .a(ID_EX_RegisterRt), .b(EX_MEM_RegisterRd), .eq(comparator_4_eq));  // open: gt, lt
  Comparator #(.width(5)) comparator_5 (
    .a(MEM_WB_RegisterRd), .b(ID_EX_RegisterRs), .eq(comparator_5_eq));  // open: gt, lt
  Comparator #(.width(5)) comparator_6 (
    .a(MEM_WB_RegisterRd), .b(ID_EX_RegisterRt), .eq(comparator_6_eq));  // open: gt, lt
  and and_3 (and_3_out, comparator_3_eq, and_1_out);
  or or_1 (FW_01, and_3_out, and_4_out);
  and and_4 (and_4_out, comparator_4_eq, and_1_out);
  and and_5 (and_5_out, and_2_out, comparator_5_eq);
  or or_2 (FW_10, and_5_out, and_6_out);
  and and_6 (and_6_out, and_2_out, comparator_6_eq);
endmodule

module DataMemory (
  input  [31:0] Address,
  input  [31:0] WriteData,
  input  in_3,
  input  in_4,
  input  Entradas,
  output [31:0] ReadData
);

  RAM #(.addrWidth(10), .bus("separate"), .Select("low")) ram_1 (
    .addr(Address[11:2]), .din(WriteData[7:0]), .data(ReadData[7:0]), .str(in_3), .clk(Entradas), .ld(in_4));  // open: sel, clr
  RAM #(.addrWidth(10), .bus("separate"), .Select("low")) ram_2 (
    .addr(Address[11:2]), .din(WriteData[15:8]), .data(ReadData[15:8]), .str(in_3), .clk(Entradas), .ld(in_4));  // open: sel, clr
  RAM #(.addrWidth(10), .bus("separate"), .Select("low")) ram_3 (
    .addr(Address[11:2]), .din(WriteData[23:16]), .data(ReadData[23:16]), .str(in_3), .clk(Entradas),
    .ld(in_4));  // open: sel, clr
  RAM #(.addrWidth(10), .bus("separate"), .Select("low")) ram_4 (
    .addr(Address[11:2]), .din(WriteData[31:24]), .data(ReadData[31:24]), .str(in_3), .clk(Entradas),
    .ld(in_4));  // open: sel, clr

  // Other names for the same wires on the sheet: Clock = Entradas; MemRead = in_4; MemWrite = in_3

  // Notes on the sheet:
  //   Salidas
endmodule

// Hazard
module Hazard_Detection_Unit (
  input  ID_EX_MemRead,
  input  [4:0] ID_EX_RegisterRT,
  input  [4:0] IF_ID_RegisterRT,
  input  [4:0] IF_ID_RegisterRS,
  output Stall
);

  wire comparator_1_eq, comparator_2_eq, or_1_out;

  Comparator #(.width(5)) comparator_1 (
    .a(ID_EX_RegisterRT), .b(IF_ID_RegisterRT), .eq(comparator_1_eq));  // open: gt, lt
  or or_1 (or_1_out, comparator_1_eq, comparator_2_eq);
  Comparator #(.width(5)) comparator_2 (
    .a(ID_EX_RegisterRT), .b(IF_ID_RegisterRS), .eq(comparator_2_eq));  // open: gt, lt
  and and_1 (Stall, ID_EX_MemRead, or_1_out);
endmodule
