// Logisim project SingleCycle_RISC-V_CPU.circ as structural Verilog: 6 circuits, main circuit main
module main (
);

  wire clock_1_out, Control_Unit_alusrc, Control_Unit_jump, Control_Unit_memread, Control_Unit_memtoreg,
       Control_Unit_memwrite, Control_Unit_pcsrc, Control_Unit_regwrite, five_stage_clock_1_out_2,
       five_stage_clock_1_out_3, five_stage_clock_1_out_4, five_stage_clock_1_out_5,
       five_stage_clock_1_out_6, five_stage_clock_1_out_7, or_1_out;
  wire [3:0] Control_Unit_aluop;
  wire [31:0] adder_1_out, alu_1_out_4, bit_extender_1_out, bit_extender_2_out, bit_extender_3_out,
       counter_1_q, Instruction_Memory_data, multiplexer_1_out, multiplexer_2_out, multiplexer_3_out,
       multiplexer_4_out, ram_1_data, register_2_q, register_3_q, register_4_q, register_5_q, register_6_q,
       register_file_1_d1, register_file_1_d2;

  Multiplexer #(.width(32), .enable("false")) multiplexer_1 (
    .in0(adder_1_out), .in1(multiplexer_2_out), .out(multiplexer_1_out), .sel(Control_Unit_pcsrc));
  Counter #(.width(32), .max('hffffffff)) counter_1 (
    .D(multiplexer_1_out), .Q(counter_1_q), .clk(five_stage_clock_1_out_2));  // open: load, count, carry, clr, preset, down
  Adder #(.width(32)) adder_1 (.a(32'h4), .b(counter_1_q), .out(adder_1_out));  // open: cin, cout
  Clock clock_1 (.out(clock_1_out));
  Five_Stage_Clock five_stage_clock_1 (
    .out_7(five_stage_clock_1_out_7), .out_2(five_stage_clock_1_out_2), .out_3(five_stage_clock_1_out_3),
    .out_4(five_stage_clock_1_out_4), .out_5(five_stage_clock_1_out_5), .out_6(five_stage_clock_1_out_6),
    .Clock(clock_1_out));
  ROM #(.dataWidth(32), .Select("low")) Instruction_Memory (.addr(counter_1_q[9:2]), .data(Instruction_Memory_data));
  Register #(.width(32), .Select("low")) register_1 (
    .D(counter_1_q), .clk(five_stage_clock_1_out_3));  // open: en, Q, clr
  Register #(.width(32), .Select("low")) register_2 (
    .D(Instruction_Memory_data), .Q(register_2_q), .clk(five_stage_clock_1_out_3));  // open: en, clr
  Control_Unit Control_Unit (
    .instr(register_2_q), .ALUOp(Control_Unit_aluop), .ALUSrc(Control_Unit_alusrc),
    .RegWrite(Control_Unit_regwrite), .MemToReg(Control_Unit_memtoreg), .PCSrc(Control_Unit_pcsrc),
    .Jump(Control_Unit_jump), .MemWrite(Control_Unit_memwrite), .MemRead(Control_Unit_memread));
  Register_File register_file_1 (
    .write_data(register_6_q), .rs1(register_2_q[24:20]), .rs2(register_2_q[19:15]),
    .in_1(Control_Unit_regwrite), .d1(register_file_1_d1), .write_register(register_2_q[11:7]),
    .d2(register_file_1_d2), .Clock(or_1_out));
  or or_1 (or_1_out, five_stage_clock_1_out_4, five_stage_clock_1_out_6);
  assign bit_extender_1_out = {{20{register_2_q[31]}}, register_2_q[31:20]};  // Bit_Extender bit_extender_1
  assign bit_extender_2_out = {{20{register_2_q[31]}}, {register_2_q[31:25], register_2_q[11:7]}};  // Bit_Extender bit_extender_2
  assign bit_extender_3_out = {{19{register_2_q[31]}}, {register_2_q[31], register_2_q[7], register_2_q[30:25], register_2_q[11:8], 1'b0}};  // Bit_Extender bit_extender_3
  Register #(.width(32), .Select("low")) register_3 (
    .D(register_file_1_d1), .Q(register_3_q), .clk(five_stage_clock_1_out_4));  // open: en, clr
  Register #(.width(32), .Select("low")) register_4 (
    .D(register_file_1_d2), .Q(register_4_q), .clk(five_stage_clock_1_out_4));  // open: en, clr
  Multiplexer #(.select(2), .width(32), .enable("false")) multiplexer_2 (
    .in0(bit_extender_1_out), .in1(bit_extender_2_out), .in2(bit_extender_3_out), .out(multiplexer_2_out));  // open: in3, sel
  Multiplexer #(.width(32), .enable("false")) multiplexer_3 (
    .in0(register_4_q), .in1(multiplexer_2_out), .out(multiplexer_3_out), .sel(Control_Unit_alusrc));
  ALU alu_1 (.out_4(alu_1_out_4), .A(register_3_q), .B(multiplexer_3_out), .ALUOp(Control_Unit_aluop));
  Register #(.width(32), .Select("low")) register_5 (
    .D(alu_1_out_4), .Q(register_5_q), .clk(five_stage_clock_1_out_5));  // open: en, clr
  RAM #(.dataWidth(32), .bus("separate"), .Select("low")) ram_1 (
    .addr(register_5_q[7:0]), .data(ram_1_data), .str(Control_Unit_memwrite), .clk(clock_1_out),
    .ld(Control_Unit_memread));  // open: din, sel, clr
  Multiplexer #(.width(32), .enable("false")) multiplexer_4 (
    .in0(register_5_q), .in1(ram_1_data), .out(multiplexer_4_out), .sel(Control_Unit_memtoreg));
  Register #(.width(32), .Select("low")) register_6 (
    .D(multiplexer_4_out), .Q(register_6_q), .clk(five_stage_clock_1_out_6));  // open: en, clr

  // Notes on the sheet:
  //   contents of Instruction_Memory (hex, n*v repeats v):
  //   7302b3
  //   R-type
  //   I-type
  //   S-type
  //   ALUsrc
endmodule

module IF_ID (
);

  wire clock_1_out;
  wire [7:0] counter_1_q_2;
  wire [31:0] adder_1_out, counter_1_q, Instruction_Memory_data, multiplexer_1_out, register_2_q;

  Multiplexer #(.width(32), .enable("false")) multiplexer_1 (
    .in0(adder_1_out), .out(multiplexer_1_out), .sel(1'b0));  // open: in1
  Counter #(.width(32), .max('hffffffff)) counter_1 (
    .D(multiplexer_1_out), .Q({counter_1_q[31:10], counter_1_q_2, counter_1_q[1:0]}), .clk(clock_1_out));  // open: load, count, carry, clr, preset, down
  Clock clock_1 (.out(clock_1_out));
  Adder #(.width(32)) adder_1 (
    .a(32'h4), .b({counter_1_q[31:10], counter_1_q_2, counter_1_q[1:0]}), .out(adder_1_out));  // open: cin, cout
  ROM #(.dataWidth(32), .Select("low")) Instruction_Memory (.addr(counter_1_q_2), .data(Instruction_Memory_data));
  Register #(.width(32), .Select("low")) register_1 (.D({counter_1_q[31:10], counter_1_q_2, counter_1_q[1:0]}));  // open: en, Q, clk, clr
  Register #(.width(32), .Select("low")) register_2 (
    .D(Instruction_Memory_data), .Q(register_2_q));  // open: en, clk, clr

  // Notes on the sheet:
  //   R-type
  //   I-type
  //   S-type
endmodule

module ALU (
  input  [31:0] A,
  input  [31:0] B,
  input  [3:0] ALUOp,
  output [31:0] out_4
);

  wire comparator_1_lt, comparator_2_lt;
  wire [31:0] adder_1_out, and_1_out, bit_extender_1_out, bit_extender_2_out, divider_1_out,
       multiplier_1_out, nand_1_out, negator_1_out, nor_1_out, not_1_out, or_1_out, shifter_1_out,
       shifter_2_out, shifter_3_out, subtractor_1_out, xor_1_out;

  Adder #(.width(32)) adder_1 (.a(A), .b(B), .out(adder_1_out));  // open: cin, cout
  Subtractor #(.width(32)) subtractor_1 (.a(A), .b(B), .out(subtractor_1_out));  // open: bin, bout
  Multiplier #(.width(32)) multiplier_1 (.a(A), .b(B), .out(multiplier_1_out));  // open: cin, cout
  Divider #(.width(32)) divider_1 (.a(A), .b(B), .out(divider_1_out));  // open: upper, rem
  assign and_1_out = A & B;  // AND_Gate and_1, 32 bits wide
  assign nand_1_out = ~(A & B);  // NAND_Gate nand_1, 32 bits wide
  assign nor_1_out = ~(A | B);  // NOR_Gate nor_1, 32 bits wide
  assign not_1_out = ~A;  // NOT_Gate not_1, 32 bits wide
  assign or_1_out = A | B;  // OR_Gate or_1, 32 bits wide
  assign xor_1_out = A ^ B;  // XOR_Gate xor_1, 32 bits wide
  Shifter #(.width(32)) shifter_1 (.in(A), .\dist (B[4:0]), .out(shifter_1_out));
  Shifter #(.width(32), .shift("lr")) shifter_2 (.in(A), .\dist (B[4:0]), .out(shifter_2_out));
  Shifter #(.width(32), .shift("ar")) shifter_3 (.in(A), .\dist (B[4:0]), .out(shifter_3_out));
  Comparator #(.width(32)) comparator_1 (.a(A), .b(B), .lt(comparator_1_lt));  // open: gt, eq
  Comparator #(.width(32), .mode("unsigned")) comparator_2 (.a(A), .b(B), .lt(comparator_2_lt));  // open: gt, eq
  Negator #(.width(32)) negator_1 (.in(A), .out(negator_1_out));
  assign bit_extender_1_out = {{31{1'b0}}, comparator_1_lt};  // Bit_Extender bit_extender_1
  assign bit_extender_2_out = {{31{1'b0}}, comparator_2_lt};  // Bit_Extender bit_extender_2
  Multiplexer #(.select(4), .width(32), .enable("false")) multiplexer_1 (
    .in0(adder_1_out), .in1(subtractor_1_out), .in2(multiplier_1_out), .in3(divider_1_out), .in4(and_1_out),
    .in5(nand_1_out), .in6(nor_1_out), .in7(not_1_out), .in8(or_1_out), .in9(xor_1_out),
    .in10(shifter_1_out), .in11(shifter_2_out), .in12(shifter_3_out), .in13(bit_extender_1_out),
    .in14(bit_extender_2_out), .in15(negator_1_out), .out(out_4), .sel(ALUOp));
endmodule

module Register_File (
  input  in_1,
  input  [4:0] rs1,
  input  [31:0] write_data,
  input  [4:0] write_register,
  input  [4:0] rs2,
  input  Clock,
  output [31:0] d1,
  output [31:0] d2
);

  wire demultiplexer_2_out0, demultiplexer_2_out1, demultiplexer_2_out2, demultiplexer_2_out3,
       demultiplexer_2_out4, demultiplexer_2_out5, demultiplexer_2_out6, demultiplexer_2_out7,
       demultiplexer_2_out8, demultiplexer_2_out9, demultiplexer_2_out10, demultiplexer_2_out11,
       demultiplexer_2_out12, demultiplexer_2_out13, demultiplexer_2_out14, demultiplexer_2_out15,
       demultiplexer_2_out16, demultiplexer_2_out17, demultiplexer_2_out18, demultiplexer_2_out19,
       demultiplexer_2_out20, demultiplexer_2_out21, demultiplexer_2_out22, demultiplexer_2_out23,
       demultiplexer_2_out24, demultiplexer_2_out25, demultiplexer_2_out26, demultiplexer_2_out27,
       demultiplexer_2_out28, demultiplexer_2_out29, demultiplexer_2_out30, demultiplexer_2_out31;
  wire [31:0] demultiplexer_1_out1, demultiplexer_1_out2, demultiplexer_1_out3, demultiplexer_1_out4,
       demultiplexer_1_out5, demultiplexer_1_out6, demultiplexer_1_out7, demultiplexer_1_out8,
       demultiplexer_1_out9, demultiplexer_1_out10, demultiplexer_1_out11, demultiplexer_1_out12,
       demultiplexer_1_out13, demultiplexer_1_out14, demultiplexer_1_out15, demultiplexer_1_out16,
       demultiplexer_1_out17, demultiplexer_1_out18, demultiplexer_1_out19, demultiplexer_1_out20,
       demultiplexer_1_out21, demultiplexer_1_out22, demultiplexer_1_out23, demultiplexer_1_out24,
       demultiplexer_1_out25, demultiplexer_1_out26, demultiplexer_1_out27, demultiplexer_1_out28,
       demultiplexer_1_out29, demultiplexer_1_out30, demultiplexer_1_out31, R1_q, R2_q, R3_q, R4_q, R5_q,
       R6_q, R7_q, R8_q, R9_q, R10_q, R11_q, R12_q, R13_q, R14_q, R15_q, R16_q, R17_q, R18_q, R19_q, R20_q,
       R21_q, R22_q, R23_q, R24_q, R25_q, R26_q, R27_q, R28_q, R29_q, R30_q, R31_q;

  Demultiplexer #(.select(5), .width(32), .enable("false")) demultiplexer_1 (
    .out1(demultiplexer_1_out1), .out2(demultiplexer_1_out2), .out3(demultiplexer_1_out3),
    .out4(demultiplexer_1_out4), .out5(demultiplexer_1_out5), .out6(demultiplexer_1_out6),
    .out7(demultiplexer_1_out7), .out8(demultiplexer_1_out8), .out9(demultiplexer_1_out9),
    .out10(demultiplexer_1_out10), .out11(demultiplexer_1_out11), .out12(demultiplexer_1_out12),
    .out13(demultiplexer_1_out13), .out14(demultiplexer_1_out14), .out15(demultiplexer_1_out15),
    .out16(demultiplexer_1_out16), .out17(demultiplexer_1_out17), .out18(demultiplexer_1_out18),
    .out19(demultiplexer_1_out19), .out20(demultiplexer_1_out20), .out21(demultiplexer_1_out21),
    .out22(demultiplexer_1_out22), .out23(demultiplexer_1_out23), .out24(demultiplexer_1_out24),
    .out25(demultiplexer_1_out25), .out26(demultiplexer_1_out26), .out27(demultiplexer_1_out27),
    .out28(demultiplexer_1_out28), .out29(demultiplexer_1_out29), .out30(demultiplexer_1_out30),
    .out31(demultiplexer_1_out31), .in(write_data), .sel(write_register));  // open: out0
  Register #(.width(32), .Select("low")) R8 (
    .D(demultiplexer_1_out15), .en(demultiplexer_2_out8), .Q(R8_q), .clk(Clock));  // open: clr
  Register #(.width(32), .Select("low")) R1 (
    .D(demultiplexer_1_out1), .en(demultiplexer_2_out1), .Q(R1_q), .clk(Clock));  // open: clr
  Register #(.width(32), .Select("low")) R9 (
    .D(demultiplexer_1_out14), .en(demultiplexer_2_out9), .Q(R9_q), .clk(Clock));  // open: clr
  Register #(.width(32), .Select("low")) R2 (
    .D(demultiplexer_1_out2), .en(demultiplexer_2_out2), .Q(R2_q), .clk(Clock));  // open: clr
  Register #(.width(32), .Select("low")) R10 (
    .D(demultiplexer_1_out13), .en(demultiplexer_2_out10), .Q(R10_q), .clk(Clock));  // open: clr
  Register #(.width(32), .Select("low")) R3 (
    .D(demultiplexer_1_out3), .en(demultiplexer_2_out3), .Q(R3_q), .clk(Clock));  // open: clr
  Register #(.width(32), .Select("low")) R11 (
    .D(demultiplexer_1_out12), .en(demultiplexer_2_out11), .Q(R11_q), .clk(Clock));  // open: clr
  Register #(.width(32), .Select("low")) R4 (
    .D(demultiplexer_1_out4), .en(demultiplexer_2_out4), .Q(R4_q), .clk(Clock));  // open: clr
  Register #(.width(32), .Select("low")) R12 (
    .D(demultiplexer_1_out11), .en(demultiplexer_2_out12), .Q(R12_q), .clk(Clock));  // open: clr
  Register #(.width(32), .Select("low")) R5 (
    .D(demultiplexer_1_out5), .en(demultiplexer_2_out5), .Q(R5_q), .clk(Clock));  // open: clr
  Register #(.width(32), .Select("low")) R13 (
    .D(demultiplexer_1_out10), .en(demultiplexer_2_out13), .Q(R13_q), .clk(Clock));  // open: clr
  Register #(.width(32), .Select("low")) R6 (
    .D(demultiplexer_1_out6), .en(demultiplexer_2_out6), .Q(R6_q), .clk(Clock));  // open: clr
  Register #(.width(32), .Select("low")) R7 (
    .D(demultiplexer_1_out7), .en(demultiplexer_2_out7), .Q(R7_q), .clk(Clock));  // open: clr
  Register #(.width(32), .Select("low")) R15 (
    .D(demultiplexer_1_out8), .en(demultiplexer_2_out15), .Q(R15_q), .clk(Clock));  // open: clr
  Register #(.width(32), .Select("low")) R14 (
    .D(demultiplexer_1_out9), .en(demultiplexer_2_out14), .Q(R14_q), .clk(Clock));  // open: clr
  Demultiplexer #(.select(5), .enable("false")) demultiplexer_2 (
    .out0(demultiplexer_2_out0), .out1(demultiplexer_2_out1), .out2(demultiplexer_2_out2),
    .out3(demultiplexer_2_out3), .out4(demultiplexer_2_out4), .out5(demultiplexer_2_out5),
    .out6(demultiplexer_2_out6), .out7(demultiplexer_2_out7), .out8(demultiplexer_2_out8),
    .out9(demultiplexer_2_out9), .out10(demultiplexer_2_out10), .out11(demultiplexer_2_out11),
    .out12(demultiplexer_2_out12), .out13(demultiplexer_2_out13), .out14(demultiplexer_2_out14),
    .out15(demultiplexer_2_out15), .out16(demultiplexer_2_out16), .out17(demultiplexer_2_out17),
    .out18(demultiplexer_2_out18), .out19(demultiplexer_2_out19), .out20(demultiplexer_2_out20),
    .out21(demultiplexer_2_out21), .out22(demultiplexer_2_out22), .out23(demultiplexer_2_out23),
    .out24(demultiplexer_2_out24), .out25(demultiplexer_2_out25), .out26(demultiplexer_2_out26),
    .out27(demultiplexer_2_out27), .out28(demultiplexer_2_out28), .out29(demultiplexer_2_out29),
    .out30(demultiplexer_2_out30), .out31(demultiplexer_2_out31), .in(in_1), .sel(write_register));
  Multiplexer #(.select(5), .enable("false")) multiplexer_1 (
    .in0(demultiplexer_2_out0), .in1(demultiplexer_2_out1), .in2(demultiplexer_2_out2),
    .in3(demultiplexer_2_out3), .in4(demultiplexer_2_out4), .in5(demultiplexer_2_out5),
    .in6(demultiplexer_2_out6), .in7(demultiplexer_2_out7), .in8(demultiplexer_2_out8),
    .in9(demultiplexer_2_out9), .in10(demultiplexer_2_out10), .in11(demultiplexer_2_out11),
    .in12(demultiplexer_2_out12), .in13(demultiplexer_2_out13), .in14(demultiplexer_2_out14),
    .in15(demultiplexer_2_out15), .in16(demultiplexer_2_out16), .in17(demultiplexer_2_out17),
    .in18(demultiplexer_2_out18), .in19(demultiplexer_2_out19), .in20(demultiplexer_2_out20),
    .in21(demultiplexer_2_out21), .in22(demultiplexer_2_out22), .in23(demultiplexer_2_out23),
    .in24(demultiplexer_2_out24), .in25(demultiplexer_2_out25), .in26(demultiplexer_2_out26),
    .in27(demultiplexer_2_out27), .in28(demultiplexer_2_out28), .in29(demultiplexer_2_out29),
    .in30(demultiplexer_2_out30), .in31(demultiplexer_2_out31));  // open: out, sel
  Multiplexer #(.select(5), .width(32), .enable("false")) multiplexer_2 (
    .in0({32{1'b0}}), .in1(R1_q), .in2(R2_q), .in3(R3_q), .in4(R4_q), .in5(R5_q), .in6(R6_q), .in7(R7_q),
    .in8(R15_q), .in9(R14_q), .in10(R13_q), .in11(R12_q), .in12(R11_q), .in13(R10_q), .in14(R9_q),
    .in15(R8_q), .in16(R16_q), .in17(R17_q), .in18(R18_q), .in19(R19_q), .in20(R20_q), .in21(R21_q),
    .in22(R22_q), .in23(R23_q), .in24(R24_q), .in25(R25_q), .in26(R26_q), .in27(R27_q), .in28(R28_q),
    .in29(R29_q), .in30(R30_q), .in31(R31_q), .out(d1), .sel(rs1));
  Multiplexer #(.select(5), .width(32), .enable("false")) multiplexer_3 (
    .in0({32{1'b0}}), .in1(R1_q), .in2(R2_q), .in3(R3_q), .in4(R4_q), .in5(R5_q), .in6(R6_q), .in7(R7_q),
    .in8(R15_q), .in9(R14_q), .in10(R13_q), .in11(R12_q), .in12(R11_q), .in13(R10_q), .in14(R9_q),
    .in15(R8_q), .in16(R16_q), .in17(R17_q), .in18(R18_q), .in19(R19_q), .in20(R20_q), .in21(R21_q),
    .in22(R22_q), .in23(R23_q), .in24(R24_q), .in25(R25_q), .in26(R26_q), .in27(R27_q), .in28(R28_q),
    .in29(R29_q), .in30(R30_q), .in31(R31_q), .out(d2), .sel(rs2));
  Register #(.width(32), .Select("low")) R16 (
    .D(demultiplexer_1_out24), .en(demultiplexer_2_out16), .Q(R16_q), .clk(Clock));  // open: clr
  Register #(.width(32), .Select("low")) R24 (
    .D(demultiplexer_1_out23), .en(demultiplexer_2_out24), .Q(R24_q), .clk(Clock));  // open: clr
  Register #(.width(32), .Select("low")) R17 (
    .D(demultiplexer_1_out25), .en(demultiplexer_2_out17), .Q(R17_q), .clk(Clock));  // open: clr
  Register #(.width(32), .Select("low")) R25 (
    .D(demultiplexer_1_out22), .en(demultiplexer_2_out25), .Q(R25_q), .clk(Clock));  // open: clr
  Register #(.width(32), .Select("low")) R18 (
    .D(demultiplexer_1_out26), .en(demultiplexer_2_out18), .Q(R18_q), .clk(Clock));  // open: clr
  Register #(.width(32), .Select("low")) R26 (
    .D(demultiplexer_1_out21), .en(demultiplexer_2_out26), .Q(R26_q), .clk(Clock));  // open: clr
  Register #(.width(32), .Select("low")) R20 (
    .D(demultiplexer_1_out28), .en(demultiplexer_2_out20), .Q(R20_q), .clk(Clock));  // open: clr
  Register #(.width(32), .Select("low")) R19 (
    .D(demultiplexer_1_out27), .en(demultiplexer_2_out19), .Q(R19_q), .clk(Clock));  // open: clr
  Register #(.width(32), .Select("low")) R28 (
    .D(demultiplexer_1_out19), .en(demultiplexer_2_out28), .Q(R28_q), .clk(Clock));  // open: clr
  Register #(.width(32), .Select("low")) R27 (
    .D(demultiplexer_1_out20), .en(demultiplexer_2_out27), .Q(R27_q));  // open: clk, clr
  Register #(.width(32), .Select("low")) R21 (
    .D(demultiplexer_1_out29), .en(demultiplexer_2_out21), .Q(R21_q), .clk(Clock));  // open: clr
  Register #(.width(32), .Select("low")) R29 (
    .D(demultiplexer_1_out18), .en(demultiplexer_2_out29), .Q(R29_q), .clk(Clock));  // open: clr
  Register #(.width(32), .Select("low")) R22 (
    .D(demultiplexer_1_out30), .en(demultiplexer_2_out22), .Q(R22_q), .clk(Clock));  // open: clr
  Register #(.width(32), .Select("low")) R30 (
    .D(demultiplexer_1_out17), .en(demultiplexer_2_out30), .Q(R30_q), .clk(Clock));  // open: clr
  Register #(.width(32), .Select("low")) R23 (
    .D(demultiplexer_1_out31), .en(demultiplexer_2_out23), .Q(R23_q), .clk(Clock));  // open: clr
  Register #(.width(32), .Select("low")) R31 (
    .D(demultiplexer_1_out16), .en(demultiplexer_2_out31), .Q(R31_q), .clk(Clock));  // open: clr
endmodule

module Five_Stage_Clock (
  input  Clock,
  output out_2,
  output out_3,
  output out_4,
  output out_5,
  output out_6,
  output out_7
);

  wire demultiplexer_1_out5, demultiplexer_1_out6, demultiplexer_1_out7;
  wire [2:0] counter_1_q;

  Counter #(.width(3), .max('h4)) counter_1 (
    .Q(counter_1_q), .clk(Clock));  // open: load, D, count, carry, clr, preset, down
  Comparator #(.width(3)) comparator_1 (.a(counter_1_q), .b(3'b000), .eq(out_7));  // open: gt, lt
  Demultiplexer #(.select(3), .enable("false")) demultiplexer_1 (
    .out0(out_2), .out1(out_3), .out2(out_4), .out3(out_5), .out4(out_6), .out5(demultiplexer_1_out5),
    .out6(demultiplexer_1_out6), .out7(demultiplexer_1_out7), .in(Clock), .sel(counter_1_q));
endmodule

module Control_Unit (
  input  [31:0] instr,
  output [3:0] ALUOp,
  output ALUSrc,
  output RegWrite,
  output MemToReg,
  output PCSrc,
  output Jump,
  output MemWrite,
  output MemRead
);

  wire and_1_out, and_2_out, and_3_out, and_4_out, and_5_out, and_6_out, and_7_out, and_8_out, and_9_out,
       and_10_out, and_11_out, and_12_out, and_13_out, and_14_out;

  and and_1 (and_1_out, instr[0], instr[1], ~instr[2], ~instr[3]);  // AND_Gate
  and and_2 (and_2_out, instr[4], instr[5], ~instr[6]);  // AND_Gate
  and and_3 (and_3_out, instr[4], ~instr[5], ~instr[6]);  // AND_Gate
  and and_4 (and_4_out, ~instr[4], ~instr[5], ~instr[6]);  // AND_Gate
  and and_5 (and_5_out, ~instr[4], instr[5], ~instr[6]);  // AND_Gate
  and and_6 (and_6_out, ~instr[4], instr[5], instr[6]);  // AND_Gate
  and and_7 (and_7_out, ~instr[4], instr[5], instr[6]);  // AND_Gate
  and and_8 (and_8_out, instr[0], instr[1], instr[2], instr[3]);
  and and_9 (and_9_out, and_1_out, and_2_out);
  and and_10 (and_10_out, and_1_out, and_3_out);
  and and_11 (and_11_out, and_1_out, and_4_out);
  and and_12 (and_12_out, and_1_out, and_5_out);
  and and_13 (and_13_out, and_1_out, and_6_out);
  and and_14 (and_14_out, and_7_out, and_8_out);
  Multiplexer #(.select(3), .enable("false")) multiplexer_1 (
    .in0(and_11_out), .in1(and_10_out), .in2(1'b0), .in3(and_9_out), .in4(1'b0), .in5(1'b0), .in6(1'b0),
    .in7(1'b0), .out(RegWrite), .sel(instr[6:4]));
  Multiplexer #(.select(3), .enable("false")) multiplexer_2 (
    .in0(and_11_out), .in1(and_10_out), .in2(and_12_out), .in3(1'b0), .in4(1'b0), .in5(1'b0),
    .in6(and_13_out), .in7(1'b0), .out(ALUSrc), .sel(instr[6:4]));
  Multiplexer #(.select(3), .enable("false")) multiplexer_3 (
    .in0(and_11_out), .in1(1'b0), .in2(1'b0), .in3(1'b0), .in4(1'b0), .in5(1'b0), .in6(1'b0), .in7(1'b0),
    .out(MemRead), .sel(instr[6:4]));
  Multiplexer #(.select(3), .enable("false")) multiplexer_4 (
    .in0(and_11_out), .in1(1'b0), .in2(1'b0), .in3(1'b0), .in4(1'b0), .in5(1'b0), .in6(1'b0), .in7(1'b0),
    .out(MemToReg), .sel(instr[6:4]));
  Multiplexer #(.select(3), .enable("false")) multiplexer_5 (
    .in0(1'b0), .in1(1'b0), .in2(and_12_out), .in3(1'b0), .in4(1'b0), .in5(1'b0), .in6(1'b0), .in7(1'b0),
    .out(MemWrite), .sel(instr[6:4]));
  Multiplexer #(.select(3), .enable("false")) multiplexer_6 (
    .in0(1'b0), .in1(1'b0), .in2(1'b0), .in3(1'b0), .in4(1'b0), .in5(1'b0), .in6(and_13_out), .in7(1'b0),
    .out(PCSrc), .sel(instr[6:4]));
  Multiplexer #(.select(3), .enable("false")) multiplexer_7 (
    .in0(1'b0), .in1(1'b0), .in2(1'b0), .in3(1'b0), .in4(1'b0), .in5(1'b0), .in6(and_14_out), .in7(1'b0),
    .out(Jump), .sel(instr[6:4]));
  or or_1 (ALUOp[0], instr[30], instr[25]);

  assign ALUOp[3:1] = instr[14:12];

  // Other names for the same wires on the sheet: funct3[2:0] = instr[14:12]; OpCode2[3:0] = instr[3:0];
  //   OpCode1[2:0] = instr[6:4]; funct7[6:0] = instr[31:25]

  // Notes on the sheet:
  //   Entradas
  //   Datapath
  //   Salidas
  //   Type-R
  //   Type-I
  //   Load
  //   Store
  //   Branch
  //   JAL
endmodule
